// Logisim project RV.circ as structural Verilog: 3 circuits, main circuit main
module main (
  input  in_1,
  input  [31:0] in_2,
  input  in_3,
  input  RESET
);

  wire CLK_out;
  wire [31:0] fetch_1_instr, fetch_1_pc, fetch_1_pc4;

  Clock CLK (.out(CLK_out));
  Fetch fetch_1 (
    .PC_SRC(in_1), .BR_TGT(in_2), .CLK(CLK_out), .RESET(RESET), .STALL_F(in_3), .PC(fetch_1_pc),
    .INSTR(fetch_1_instr), .PC4(fetch_1_pc4));
  Decode decode_1 (
    .PC(fetch_1_pc), .INSTR(fetch_1_instr), .PC4(fetch_1_pc4), .CLK(CLK_out), .RESET(RESET));  // open: STALL_D
endmodule

module Fetch (
  input  PC_SRC,
  input  [31:0] BR_TGT,
  input  CLK,
  input  RESET,
  input  STALL_F,
  output [31:0] PC,
  output [31:0] INSTR,
  output [31:0] PC4
);

  wire [31:0] multiplexer_1_out;

  Register #(.width(32)) PC_REG (.D(multiplexer_1_out), .en(STALL_F), .clk(CLK), .Q(PC), .clr(RESET));
  Multiplexer #(.width(32)) multiplexer_1 (.in0(PC4), .in1(BR_TGT), .out(multiplexer_1_out), .sel(PC_SRC));
  Adder #(.width(32)) adder_1 (.a(PC), .b(32'h4), .out(PC4));  // open: cin, cout
  ROM #(.addrWidth(16), .dataWidth(32)) IMEM (.addr(PC[17:2]), .data(INSTR));
endmodule

module Decode (
  input  [31:0] PC,
  input  [31:0] INSTR,
  input  [31:0] PC4,
  input  CLK,
  input  RESET,
  input  STALL_D
);

  Register #(.width(32)) register_1 (.D(PC), .en(STALL_D), .clk(CLK), .clr(RESET));  // open: Q
  Register #(.width(32)) register_2 (.D(INSTR), .en(STALL_D), .clk(CLK), .clr(RESET));  // open: Q
  Register #(.width(32)) register_3 (.D(PC4), .en(STALL_D), .clk(CLK), .clr(RESET));  // open: Q
endmodule
